# Fritzing sketch m-a-p (saved by Fritzing 0.9.10b)
breadboards: 2

parts:
  Composant1 = Arduino Uno (Rev3)
  A1 = 2 channel relay module [package=THT]
  DHT1 = DHT11 Humitidy and Temperature Sensor
  Composant2 = FC-28 Soil Hygrometer Module
  Composant3 = FC-28 Soil Hygrometer Module - Probe
  U1 = Breadboard Power Supply [package=THT]
  Water_Level_Sensor1 = Water Level Sensor
  Pompe = DC Motor [voltage_(max)=6V voltage_(min)=3V]
  résistance_chauffante = Resistor [tolerance=±5% power=0.25 resistance=1G package=THT]

nets:
  N1: Composant1.A0, Composant2.VCC
  N2: Composant1.A1, Water_Level_Sensor1.SIG
  N3: Composant1.D11_PWM/MOSI, A1.pin_11
  N4: Composant1.D12/MISO, A1.pin_8
  N5: Composant1.D2, DHT1.DATA
  GND: Composant1.GND, DHT1.GND
  N6: A1.pin_1, Pompe.pin_1
  N7: A1.pin_4, résistance_chauffante.Pin_1
  N8: A1.pin_13, DHT1.VDD
  N9: A1.pin_14, U1.pin1, U1.pin2, Pompe.pin_2, résistance_chauffante.Pin_0
  N10: Composant2.DO, U1.pin5, U1.pin6, Water_Level_Sensor1.GND
  N11: Composant2.AO, Water_Level_Sensor1.VCC
  N12: Composant2.POS, Composant3.POS
  N13: Composant2.NEG, Composant3.NEG
  N14: U1.pin3, U1.pin4
  N15: U1.pin7, U1.pin8

custom parts:
  2 channel relay module: 2 channel Relay Module 5V 12V 24V High and Low Level Trigger Relay Control With Optocoupler Two Way relays DC 5 V 12 V 24 V Volt.
  DHT11 Humitidy and Temperature Sensor: DHT11 Humidity and Temperature Sensor
  FC-28 Soil Hygrometer Module: The FC-28 is a soil hygrometer module that uses the Texas Instruments LM393 comparator chip to provide an analog measurement of soil humidity. The digital output is high when soil moisture is over a certain threshold, as determined by adjusting the potentiometer.
  FC-28 Soil Hygrometer Module - Probe: The FC-28 is a soil hygrometer module that uses the Texas Instruments LM393 comparator chip to provide an analog measurement of soil humidity.
  Breadboard Power Supply: Représentation Carte Breadboard Power Supply
  Water Level Sensor: A water level sensor. This sensor operates at 3V to 5V. The Sig (signal) pin outputs an analogue signal that is in proportion to the amount of water in contact with the sensor.
